# Fritzing sketch Untitled Sketch2 (saved by Fritzing 0.9.1b)
perfboards: 1

parts:
  Q1 = NPN-Transistor [package="TO92 [THT]"]
  J1 = female pin header, 2 pins [form="♀ (female)"]
  J4 = female pin header, 2 pins [form="♀ (female)"]
  J3 = female pin header, 2 pins [form="♀ (female)"]
  J5 = female pin header, 2 pins [form="♀ (female)"]
  J8 = female pin header, 2 pins [form="♀ (female)"]
  J7 = female pin header, 2 pins [form="♀ (female)"]
  J9 = female pin header, 2 pins [form="♀ (female)"]
  J6 = female pin header, 2 pins [form="♀ (female)"]
  LED1 = LED - 3mm [color="Red (633nm)" package="3 mm [THT]"]
  R1 = Resistor [tolerance=±5% resistance=220 package=THT]

nets:
  N1: Q1.E, J4.pin1
  N2: Q1.B, LED1.cathode
  N3: J1.pin1, J7.pin1
  N4: J3.pin2, J6.pin2
  N5: J5.pin1, J6.pin1
  N6: J5.pin2, J9.pin2
  N7: J8.pin1, R1.Pin_0
  N8: LED1.anode, R1.Pin_1
